// Logisim project Bank Counter.circ as structural Verilog: 3 circuits, main circuit main
module main (
  input  [1:0] Mode,
  input  [3:0] Load_Input_1,
  input  [3:0] Load_Input_2,
  input  [3:0] Load_Input_3
);

  wire A_Bank_Counter_out, and_1_out, B_Bank_Counter_out, button_fence_1_output, button_fence_2_output,
       button_fence_3_output, button_fence_4_output, C_Bank_Counter_out, Clock_out, Counter_2_carry,
       D_Bank_Counter_out, d_ff_1_q, decoder_1_out0, decoder_1_out1, logic_1_a, logic_1_b, logic_1_c,
       logic_1_d, logic_1_e, logic_1_f, logic_1_g, logic_2_a, logic_2_b, logic_2_c, logic_2_d, logic_2_e,
       logic_2_f, logic_2_g, or_1_out, or_2_out;
  wire [3:0] Counter_1_q, Counter_2_q, multiplexer_1_out, priority_encoder_1_out;
  wire [6:0] rom_1_data, rom_2_data, rom_3_data, rom_4_data, rom_5_data;

  Button A_Bank_Counter (.out(A_Bank_Counter_out));
  Button B_Bank_Counter (.out(B_Bank_Counter_out));
  Button C_Bank_Counter (.out(C_Bank_Counter_out));
  Button D_Bank_Counter (.out(D_Bank_Counter_out));
  Decoder #(.select(2), .enable("false")) decoder_1 (
    .out0(decoder_1_out0), .out1(decoder_1_out1), .sel(Mode));  // open: out2, out3
  Button_fence button_fence_1 (.\input (A_Bank_Counter_out), .\output (button_fence_1_output));
  Button_fence button_fence_2 (.\input (B_Bank_Counter_out), .\output (button_fence_2_output));
  Button_fence button_fence_3 (.\input (C_Bank_Counter_out), .\output (button_fence_3_output));
  Button_fence button_fence_4 (.\input (D_Bank_Counter_out), .\output (button_fence_4_output));
  or or_1 (or_1_out, button_fence_1_output, button_fence_2_output, button_fence_3_output, button_fence_4_output);
  Clock Clock (.out(Clock_out));
  D_Flip_Flop d_ff_1 (.clk(Clock_out), .D(1'b0), .Q(d_ff_1_q), .preset(decoder_1_out0));  // open: Qn, en, reset
  and and_1 (and_1_out, or_1_out, Counter_2_carry);
  Counter #(.width(4), .max('h9)) Counter_2 (
    .load(d_ff_1_q), .D(Load_Input_2), .count(or_1_out), .Q(Counter_2_q), .carry(Counter_2_carry),
    .clk(Clock_out));  // open: clr
  Counter #(.width(4), .max('h9)) Counter_1 (
    .load(d_ff_1_q), .D(Load_Input_1), .count(and_1_out), .Q(Counter_1_q), .clk(Clock_out));  // open: carry, clr
  Priority_Encoder #(.select(4)) priority_encoder_1 (
    .in0(button_fence_1_output), .in1(button_fence_2_output), .in2(button_fence_3_output),
    .in3(button_fence_4_output), .in4(1'b0), .in5(1'b0), .in6(1'b0), .in7(1'b0), .in8(1'b0), .in9(1'b0),
    .in10(1'b0), .in11(1'b0), .in12(1'b0), .in13(1'b0), .in14(1'b0), .in15(1'b0), .out(priority_encoder_1_out));  // open: gs, en_out, en_in
  Logic logic_1 (
    .ABCD(Counter_2_q), .a(logic_1_a), .b(logic_1_b), .c(logic_1_c), .d(logic_1_d), .e(logic_1_e),
    .f(logic_1_f), .g(logic_1_g));
  Logic logic_2 (
    .ABCD(Counter_1_q), .a(logic_2_a), .b(logic_2_b), .c(logic_2_c), .d(logic_2_d), .e(logic_2_e),
    .f(logic_2_f), .g(logic_2_g));
  or or_2 (or_2_out, decoder_1_out1, d_ff_1_q);
  _7_Segment_Display u_7_segment_display_1 (
    .g(logic_2_g), .f(logic_2_f), .a(logic_2_a), .b(logic_2_b), .e(logic_2_e), .d(logic_2_d), .c(logic_2_c));  // open: dp
  Multiplexer #(.width(4), .enable("false")) multiplexer_1 (
    .in0(priority_encoder_1_out), .in1(Load_Input_3), .out(multiplexer_1_out), .sel(or_2_out));
  _7_Segment_Display u_7_segment_display_2 (
    .g(logic_1_g), .f(logic_1_f), .a(logic_1_a), .b(logic_1_b), .e(logic_1_e), .d(logic_1_d), .c(logic_1_c));  // open: dp
  DotMatrix dotmatrix_1 (.col0(rom_1_data), .col1(rom_2_data), .col2(rom_3_data), .col3(rom_4_data), .col4(rom_5_data));
  ROM #(.addrWidth(4), .dataWidth(7)) rom_1 (.addr(multiplexer_1_out), .data(rom_1_data));  // open: sel
  ROM #(.addrWidth(4), .dataWidth(7)) rom_2 (.addr(multiplexer_1_out), .data(rom_2_data));  // open: sel
  ROM #(.addrWidth(4), .dataWidth(7)) rom_3 (.addr(multiplexer_1_out), .data(rom_3_data));  // open: sel
  ROM #(.addrWidth(4), .dataWidth(7)) rom_4 (.addr(multiplexer_1_out), .data(rom_4_data));  // open: sel
  ROM #(.addrWidth(4), .dataWidth(7)) rom_5 (.addr(multiplexer_1_out), .data(rom_5_data));  // open: sel

  // Notes on the sheet:
  //   Mode 0 - Custom Input
  //   Mode 1 - Single Counter
  //   Mode 2/3 - Multiple Counter
  //   Tick Frequency = 64Hz
  //   Logic
  //   Logic
  //   contents of rom_1 (hex, n*v repeats v):
  //   1f 41 3e 41 7f 7f 3e 9*20
  //   contents of rom_2 (hex, n*v repeats v):
  //   24 7f 41 7f 49 48 41 9*40
  //   contents of rom_3 (hex, n*v repeats v):
  //   44 49 41 41 49 48 41 9*45
  //   contents of rom_4 (hex, n*v repeats v):
  //   24 49 41 41 49 48 49 9*48
  //   contents of rom_5 (hex, n*v repeats v):
  //   1f 36 22 3e 41 40 2e 9*30
endmodule

module Logic (
  input  [3:0] ABCD,
  output a,
  output b,
  output c,
  output d,
  output e,
  output f,
  output g
);

  wire and_1_out, and_2_out, and_3_out, and_4_out, and_5_out, and_6_out, and_7_out, and_8_out, and_9_out,
       and_10_out, and_11_out, and_12_out, and_13_out, and_14_out, and_15_out, and_16_out, and_17_out,
       not_1_out, not_2_out, not_3_out, not_4_out, not_5_out, not_6_out, not_7_out, not_8_out, not_9_out,
       not_10_out, not_11_out, not_12_out, not_13_out, not_14_out, not_15_out, not_16_out, not_17_out,
       not_18_out, not_19_out, not_20_out, not_21_out, or_1_out, or_2_out, or_3_out, or_4_out, or_6_out,
       or_8_out, or_9_out, or_10_out, or_11_out, or_14_out, or_15_out;

  not not_1 (not_1_out, ABCD[2]);
  not not_2 (not_2_out, ABCD[0]);
  not not_3 (not_3_out, ABCD[1]);
  not not_4 (not_4_out, ABCD[0]);
  not not_5 (not_5_out, ABCD[1]);
  not not_6 (not_6_out, ABCD[2]);
  not not_7 (not_7_out, ABCD[0]);
  not not_8 (not_8_out, ABCD[2]);
  not not_9 (not_9_out, ABCD[1]);
  not not_10 (not_10_out, ABCD[2]);
  not not_11 (not_11_out, ABCD[0]);
  not not_12 (not_12_out, ABCD[0]);
  not not_13 (not_13_out, ABCD[1]);
  not not_14 (not_14_out, ABCD[0]);
  not not_15 (not_15_out, ABCD[1]);
  not not_16 (not_16_out, ABCD[0]);
  not not_17 (not_17_out, ABCD[2]);
  not not_18 (not_18_out, ABCD[1]);
  not not_19 (not_19_out, ABCD[0]);
  and and_1 (and_1_out, not_1_out, not_2_out);
  and and_2 (and_2_out, ABCD[2], ABCD[0]);
  not not_20 (not_20_out, ABCD[2]);
  and and_3 (and_3_out, not_3_out, not_4_out);
  or or_1 (or_1_out, not_5_out, ABCD[0]);
  and and_4 (and_4_out, not_6_out, not_7_out);
  and and_5 (and_5_out, not_8_out, ABCD[1]);
  not not_21 (not_21_out, ABCD[0]);
  and and_6 (and_6_out, ABCD[2], not_9_out);
  and and_7 (and_7_out, not_10_out, not_11_out);
  and and_8 (and_8_out, ABCD[1], not_12_out);
  and and_9 (and_9_out, not_13_out, not_14_out);
  and and_10 (and_10_out, ABCD[2], not_15_out);
  and and_11 (and_11_out, ABCD[2], not_16_out);
  and and_12 (and_12_out, not_17_out, ABCD[1]);
  and and_13 (and_13_out, ABCD[2], not_18_out);
  and and_14 (and_14_out, ABCD[2], not_19_out);
  or or_2 (or_2_out, and_1_out, ABCD[1]);
  or or_3 (or_3_out, and_2_out, ABCD[3]);
  or or_4 (or_4_out, not_20_out, and_3_out);
  and and_15 (and_15_out, ABCD[1], ABCD[0]);
  or or_5 (c, or_1_out, ABCD[2]);
  or or_6 (or_6_out, and_4_out, and_5_out);
  and and_16 (and_16_out, ABCD[1], not_21_out);
  and and_17 (and_17_out, and_6_out, ABCD[0]);
  or or_7 (e, and_7_out, and_8_out);
  or or_8 (or_8_out, and_9_out, and_10_out);
  or or_9 (or_9_out, and_11_out, ABCD[3]);
  or or_10 (or_10_out, and_12_out, and_13_out);
  or or_11 (or_11_out, and_14_out, ABCD[3]);
  or or_12 (a, or_2_out, or_3_out);
  or or_13 (b, or_4_out, and_15_out);
  or or_14 (or_14_out, or_6_out, and_16_out);
  or or_15 (or_15_out, and_17_out, ABCD[3]);
  or or_16 (f, or_8_out, or_9_out);
  or or_17 (g, or_10_out, or_11_out);
  or or_18 (d, or_14_out, or_15_out);
endmodule

module Button_fence (
  input  \input ,
  output \output 
);

  wire A_q, A_qn, and_1_out, and_2_out, and_3_out, B_q, B_qn, clk_out, or_1_out;

  Clock clk (.out(clk_out));
  D_Flip_Flop A (.clk(clk_out), .D(and_1_out), .Q(A_q), .Qn(A_qn));  // open: preset, en, reset
  D_Flip_Flop B (.clk(clk_out), .D(and_2_out), .Q(B_q), .Qn(B_qn));  // open: preset, en, reset
  or or_1 (or_1_out, A_q, B_q);
  and and_1 (and_1_out, or_1_out, \input );
  and and_2 (and_2_out, \input , A_qn, B_qn);
  and and_3 (and_3_out, A_q, B_q);
  or or_2 (\output , and_2_out, and_3_out);
endmodule
